# Fritzing sketch lab05 (saved by Fritzing 0.9.3b)
breadboards: 1

parts:
  Raspberry_Pi_1 = Raspberry Pi 3 [part_number=RPI-3-V1.2]
  S1 = Pushbutton [package="[THT]"]
  R1 = Resistor [tolerance=±5% resistance=220 package=THT]
  J1 = Basic Servo

nets:
  GND: Raspberry_Pi_1.GND, S1.Pin_1, S1.Pin_2, J1.gnd
  N1: Raspberry_Pi_1.GIPO12, S1.Pin_3, S1.Pin_4
  N2: Raspberry_Pi_1.GIPO18, R1.Pin_1
  5V: Raspberry_Pi_1.5V, J1.vcc
  N3: R1.Pin_0, J1.pulse
